# Fritzing sketch Gas Sensor (saved by Fritzing 0.9.10b)
breadboards: 1

parts:
  U1 = GAS_SENSOR [package=mq-3]
  R3 = Trimmer Potentiometer [maximum_resistance=10kΩ knob_status=50% power=0.5W package=THT]
  R4 = Resistor [tolerance=±5% resistance=220 power=0.25 package=THT]
  LCD1 = LCD screen

nets:
  VSS: U1.H1, R3.leg1, R3.leg2, R4.Pin_0, LCD1.VSS, LCD1.VDD, LCD1.R/W, LCD1.LED-
  N1: R3.wiper, LCD1.V0
  N2: R4.Pin_1, LCD1.LED+
  N3: LCD1.DB6, LCD1.DB7
