# Fritzing sketch batan (saved by Fritzing 0.9.2b)

parts:
  Part1 = Adafruit ADS1115 16Bit I2C ADC [part_number="Adafruit ADS1115"]
  Part2 = Adafruit ADS1115 16Bit I2C ADC [part_number="Adafruit ADS1115"]
  Component1 = RS485_XY-017 [part_number="XY-017 TTL RS485 3V3 5V"]
  RHT1 = Humidity and Temperature Sensor RHT03 [part_number="DHT11 Humidity and Tmperature"]
  Part3 = KY-019 5V Relay Module [part_number="Solid State Relay 5V" package="Breakout board"]
  DS1 = DS18B20 1-Wire Temperature Sensor [part_number="DS18B20 Temp Sensor"]
  U2 = Mini-360 DC-DC Buck converter [part_number="DC-DC Buck Converter 4-24V-> 5V" package=THT]
  R1 = Resistor [tolerance=±5% resistance=4.7k package="2010 [SMD]"]
  Part4 = ACS712 Current Sensor Module [part_number="ACS712 20A Hall Current"]
  Part5 = ACS712 Current Sensor Module [part_number="ACS712 20A Hall Current"]
  Part6 = ACS712 Current Sensor Module [part_number="ACS712 20A Hall Current"]
  Part7 = ACS712 Current Sensor Module [part_number="ACS712 20A Hall Current"]
  Part8 = ACS712 Current Sensor Module [part_number="ACS712 20A Hall Current"]
  Part9 = Voltage Sensor Module [part_number="Voltage Sensor Module 0-24V->5V"]
  BAT1 = 18650 battery holder [part_number="24V 6S6P Lithium" package=battery-18650-kit]
  BAT2 = 18650 battery holder [part_number="24V 6S6P Lithium" package=battery-18650-kit]
  BAT3 = 18650 battery holder [part_number="24V 6S6P Lithium" package=battery-18650-kit]
  BAT4 = 18650 battery holder [part_number="24V 6S6P Lithium" package=battery-18650-kit]
  BAT5 = 18650 battery holder [part_number="24V 6S6P Lithium" package=battery-18650-kit]
  Part10 = Solar Charge Controller [part_number="Epever Tracer 2206AN 20A MPPT Solar Controller" package=PWM-Model]
  Part11 = Solar Panel [part_number="Solar Panels 24V 500W" package="Renogy 50 Watts 12 Volt Monocrystalline Bendable Solar Panel"]
  U3 = RJ45 Jack [part_number="Charger Comms RS485" package=rj45-8]
  U1 = D-DUINO
  J1 = Screw terminal - 2 pins [part_number="LOAD or INVERTER" package=THT]

nets:
  N1: Part1.AIN3, Part6.OUT
  N2: Part1.AIN2, Part5.OUT
  N3: Part1.AIN1, Part4.OUT
  VCC: Part1.AIN0, Part1.VDD, Part2.VDD, Part3.+, U2.OUT+, Part4.VCC, Part5.VCC, Part6.VCC, Part7.VCC, Part8.VCC, Part9.VCC, U1.Vin
  GND: Part1.ADDR, Part1.GND, Part2.GND, Component1.RXD, Part3.-, U2.OUT-, Part4.GND, Part5.GND, Part6.GND, Part7.GND, Part8.GND, Part9.GND, U1.D4, U1.GND#14
  N4: Part1.SDA, Part2.ADDR, Part2.SDA, U1.D1
  N5: Part1.SCL, Part2.SCL, U1.D2
  N6: Part2.AIN2, Part9.OUT
  N7: Part2.AIN1, Part8.OUT
  N8: Part2.AIN0, Part7.OUT
  N9: Component1.GND#0, RHT1.Data-signal, DS1.GND, U1.D5, U1.GND#13, U1.SD0
  N10: Component1.A, U3.3
  N11: Component1.B, U3.5
  VCC_2: Component1.VCC, DS1.VDD, R1.Pin_1, U1.3V3#12
  N12: Component1.TXD, U1.D3
  N13: Component1.GND#5, U3.7
  N14: RHT1.Vcc, U1.3V3#18
  N15: RHT1.GND_2, U1.GND#17
  N16: Part3.S, U1.D6
  N17: DS1.DQ, R1.Pin_0, U1.D7
  N18: U2.IN-, Part4.INPUT+, Part5.INPUT+, Part6.INPUT+, Part7.INPUT+, Part8.INPUT+, Part9.INPUT-, Part10.Connector_4, J1.pin2
  N19: U2.IN+, Part9.INPUT+, BAT1.+, BAT2.+, BAT3.+, BAT4.+, BAT5.+, Part10.Connector_3, J1.pin1
  N20: Part4.INPUT-, BAT1.-
  N21: Part5.INPUT-, BAT2.-
  N22: Part6.INPUT-, BAT3.-
  N23: Part7.INPUT-, BAT4.-
  N24: Part8.INPUT-, BAT5.-
  N25: Part10.Connector_1, Part11.Connector_1
  N26: Part10.Connector_2, Part11.Connector_2

notes:
  [BatAn] Battery Bank Analyzer
  Iñigo Otsoa 2019 iotsoa@gmail.com

custom parts:
  Adafruit ADS1115 16Bit I2C ADC: For microcontrollers without an analog-to-digital converter or when you want a higher-precision ADC, the ADS1115 provides 16-bit precision at 860 samples/second over I2C. The chip can be configured as 4 single-ended input channels, or two differential channels. As a nice bonus, it even includes a programmable gain amplifier, up to x16, to help boost up smaller single/differential signals to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
  RS485_XY-017: Commercially available RS485 to RS232 TTL Module
  KY-019 5V Relay Module: KY-019 5V Relay module, used to control AC circuits.
  Mini-360 DC-DC Buck converter: Mini-360 DC-DC Buck converter. Tiny buck step down voltage converter, input voltage 4.75 to 23V output 1 to 17V adjustable. Available from ebay and the like.
  18650 battery holder: 18650 Battery Holder
  Solar Charge Controller: PWM-Solar Charge Controller
  Solar Panel: Renogy 50 Watts 12 Volt Solar Panel
  D-DUINO: ESP8266 based NodeMCU with OLED display
